// Logisim project Cableado_CU (4).circ as structural Verilog: 1 circuit, main circuit main
module main (
);

  wire clock_1_out, clock_2_out, clock_3_out, clock_4_out, clock_5_out, clock_6_out, clock_7_out,
       clock_8_out, clock_9_out, clock_10_out;
  wire [3:0] register_1_q;
  wire [7:0] adder_2_out, alu_1_out_6, B_q, multiplexer_1_out, register_2_q;
  wire [11:0] adder_1_out, IR_LOW_q, MAR_q, PC_q;
  wire [15:0] A_q, MBR_q, ram_1_dout, rom_1_data, rom_2_data;

  Register #(.width(12)) PC (.D(adder_1_out), .en(rom_2_data[8]), .clk(clock_1_out), .Q(PC_q));  // open: clr
  Clock clock_1 (.out(clock_1_out));
  Adder #(.width(12)) adder_1 (.a(12'h1), .b(PC_q), .out(adder_1_out));  // open: cin, cout
  ROM #(.addrWidth(12), .dataWidth(16)) rom_1 (.addr(PC_q), .data(rom_1_data));
  Register #(.width(16)) MBR (.D(rom_1_data), .en(rom_2_data[9]), .clk(clock_2_out), .Q(MBR_q));  // open: clr
  Clock clock_2 (.out(clock_2_out));
  Register #(.width(4)) IR_HI (
    .D(MBR_q[15:12]), .en(rom_2_data[3]), .clk(clock_3_out), .Q(adder_2_out[7:4]));  // open: clr
  Clock clock_3 (.out(clock_3_out));
  Register #(.width(12)) IR_LOW (.D(MBR_q[11:0]), .en(rom_2_data[4]), .clk(clock_4_out), .Q(IR_LOW_q));  // open: clr
  Clock clock_4 (.out(clock_4_out));
  Register #(.width(4)) register_1 (
    .D(adder_2_out[3:0]), .en(1'b1), .clk(clock_5_out), .Q(register_1_q), .clr(rom_2_data[14]));
  Clock clock_5 (.out(clock_5_out));
  Register #(.width(12)) MAR (.D(IR_LOW_q), .en(rom_2_data[2]), .clk(clock_6_out), .Q(MAR_q));  // open: clr
  Clock clock_6 (.out(clock_6_out));
  Adder #(.width(4)) adder_2 (.a(4'b0001), .b(register_1_q), .out(adder_2_out[3:0]));  // open: cin, cout
  Clock clock_7 (.out(clock_7_out));
  ROM #(.dataWidth(16)) rom_2 (.addr(adder_2_out), .data(rom_2_data));
  RAM #(.addrWidth(12), .dataWidth(16)) ram_1 (
    .addr(MAR_q), .we(rom_2_data[0]), .oe(rom_2_data[1]), .clk(clock_7_out), .din(A_q), .dout(ram_1_dout));
  Multiplexer #(.width(8)) multiplexer_1 (
    .in0(alu_1_out_6), .in1(ram_1_dout[7:0]), .out(multiplexer_1_out), .sel(rom_2_data[7]));
  Register B (.D(ram_1_dout[7:0]), .en(rom_2_data[5]), .clk(clock_8_out), .Q(B_q));  // open: clr
  Clock clock_8 (.out(clock_8_out));
  Register A (.D(multiplexer_1_out), .en(rom_2_data[6]), .clk(clock_9_out), .Q(A_q[7:0]));  // open: clr
  Clock clock_9 (.out(clock_9_out));
  ALU alu_1 (.in_1(rom_2_data[12:10]), .in_2(A_q[7:0]), .in_3(B_q), .out_6(alu_1_out_6));  // open: in_4, out_5
  Register register_2 (.D(alu_1_out_6), .en(rom_2_data[13]), .clk(clock_10_out), .Q(register_2_q));  // open: clr
  Clock clock_10 (.out(clock_10_out));
  _7_Segment_Display u_7_segment_display_1 ();  // open: g, f, a, b, e, d, c, dp
  // BCD_to_7_Segment_decoder bcd_to_7_segment_decoder_1: pin names not known
  // Binary_to_BCD_converter #(.binvalue(8)) binary_to_bcd_converter_1: pin names not known; wires that end beside it: register_2_q
  _7_Segment_Display u_7_segment_display_2 ();  // open: g, f, a, b, e, d, c, dp
  _7_Segment_Display u_7_segment_display_3 ();  // open: g, f, a, b, e, d, c, dp
  // BCD_to_7_Segment_decoder bcd_to_7_segment_decoder_2: pin names not known
  // BCD_to_7_Segment_decoder bcd_to_7_segment_decoder_3: pin names not known

  // Notes on the sheet:
  //   contents of rom_1 (hex, n*v repeats v):
  //   5000 2014 5001 2015 2015 201e 2014 301e 2016 2016 201e 2015 301e 2017 2017 201e 2016 301e 2018 8000
  //   contents of rom_2 (hex, n*v repeats v):
  //   0 200 18 4 3 c0 20 2000 4000
endmodule
